# Fritzing sketch RaspberryPi-PCA9685-Servo Connection (saved by Fritzing 0.9.3b)

parts:
  Raspberry_Pi1 = Raspberry Pi 2
  PWM1 = PCA9685 16x12-bit PWM Breakout
  J1 = Basic Servo
  DC1 = DC_DC_XL4016 [package=board_screw]  # not connected
  VCC1 = Battery  # not connected

nets:
  N1: Raspberry_Pi1.3v3, PWM1.no_name_yet#505
  N2: Raspberry_Pi1.GPIO2, PWM1.no_name_yet#504
  N3: Raspberry_Pi1.GPIO3, PWM1.no_name_yet#503
  GND: Raspberry_Pi1.GND, PWM1.no_name_yet#501, PWM1.no_name_yet#1000, J1.gnd
  N4: PWM1.no_name_yet#0, J1.pulse
  N5: PWM1.no_name_yet#100, J1.vcc
